# Fritzing sketch circuit diagram (saved by Fritzing 0.9.3b)
breadboards: 1

parts:
  U1 = NodeMCU V1.0
  hc-sr1 = hc-sr04
  hc-sr2 = hc-sr04
  VCC2 = 4 x AAA Battery Mount
  U2 = NodeMCU V1.0
  R2 = Resistor [tolerance=±5% resistance=220 package="0805 [SMD]"]
  R3 = Resistor [tolerance=±5% resistance=220 package="0402 [SMD]"]
  R4 = Resistor [tolerance=±5% resistance=220 package="0805 [SMD]"]
  R5 = Resistor [tolerance=±5% resistance=220 package="0402 [SMD]"]
  U3 = 2-Channel 5v Relay Shield [package=relay-2ch5v10a]
  VCC3 = 4 x AAA Battery Mount  # not connected
  S2 = SWITCH-DPDT [package=ms]

nets:
  N1: U1.D1, hc-sr1.Trig
  N2: U1.D2, R2.Pin_1, R3.Pin_0
  N3: U1.D3, hc-sr2.Trig
  N4: U1.D4, R4.Pin_1, R5.Pin_0
  GND: U1.GND, hc-sr1.GND, hc-sr2.GND, VCC2.-, R3.Pin_1, R5.Pin_1, U3.GND
  N5: U1.D7, U3.IN1
  N6: U1.D8, U3.IN2
  VCC: U1.Vin, hc-sr1.VCC, hc-sr2.VCC, VCC2.+, U3.VCC
  N7: hc-sr1.Echo, R2.Pin_0
  N8: hc-sr2.Echo, R4.Pin_0
  N9: U2.Vin, S2.5

custom parts:
  NodeMCU V1.0: ESP8266 based NodeMCU
  2-Channel 5v Relay Shield: 2 Channel 5v Relay Shield w. 2x SPD-06VDC-SD-C
